// Logisim project Digital Clock (1).circ as structural Verilog: 1 circuit, main circuit main
module main (
);

  wire A_2_out, A_3_out, A_4_out, A_5_out, A_nC_2_out, A_nC_out, A_nD_out, A_out, and_1_out, and_2_out,
       and_3_out, and_4_out, and_5_out, and_6_out, B_2_out, B_3_out, B_4_out, B_5_out, B_nC_2_out,
       B_nC_3_out, B_nC_4_out, B_nC_5_out, B_nC_6_out, B_nC_out, B_nD_2_out, B_nD_3_out, B_nD_4_out,
       B_nD_5_out, B_nD_6_out, B_nD_out, B_out, BC_out, BD_2_out, BD_3_out, BD_4_out, BD_5_out, BD_out,
       C_2_out, C_3_out, C_4_out, C_5_out, C_nD_2_out, C_nD_3_out, C_nD_4_out, C_nD_5_out, C_nD_6_out,
       C_nD_7_out, C_nD_8_out, C_nD_9_out, C_nD_out, C_out, CD_2_out, CD_3_out, CD_4_out, CD_5_out, CD_out,
       clock_1_out, D_2_out, D_3_out, D_4_out, D_5_out, d_ff_1_q, d_ff_1_qn, d_ff_2_q, d_ff_2_qn, d_ff_3_q,
       d_ff_3_qn, d_ff_4_q, d_ff_4_qn, d_ff_5_q, d_ff_5_qn, d_ff_6_q, d_ff_6_qn, d_ff_7_q, d_ff_7_qn,
       d_ff_8_q, d_ff_8_qn, d_ff_9_q, d_ff_9_qn, d_ff_10_q, d_ff_10_qn, d_ff_11_q, d_ff_11_qn, d_ff_12_q,
       d_ff_12_qn, d_ff_13_q, d_ff_13_qn, d_ff_14_q, d_ff_14_qn, d_ff_15_q, d_ff_15_qn, d_ff_16_q,
       d_ff_16_qn, d_ff_17_q, d_ff_17_qn, d_ff_18_q, d_ff_18_qn, d_ff_19_qn, D_out, E_2_out, E_3_out,
       E_4_out, E_5_out, E_out, F_2_out, F_3_out, F_4_out, F_5_out, F_out, G_2_out, G_3_out, G_4_out,
       G_5_out, G_out, nA_nBC_out, nAC_out, nB_nCD_2_out, nB_nCD_3_out, nB_nCD_4_out, nB_nCD_5_out,
       nB_nCD_out, nB_nD_2_out, nB_nD_3_out, nB_nD_4_out, nB_nD_5_out, nB_nD_6_out, nB_nD_7_out, nB_nD_8_out,
       nB_nD_9_out, nB_nD_10_out, nB_nD_out, nB_out, nBC_2_out, nBC_3_out, nBC_4_out, nBC_5_out, nBC_6_out,
       nBC_7_out, nBC_8_out, nBC_out, nC_nD_2_out, nC_nD_3_out, nC_nD_4_out, nC_nD_5_out, nC_nD_6_out,
       nC_nD_7_out, nC_nD_8_out, nC_nD_9_out, nC_nD_10_out, nC_nD_out, nC_out, nD_out, not_1_out, not_2_out,
       not_3_out, not_4_out, not_5_out, not_6_out, not_7_out, not_8_out, not_9_out, not_10_out, not_11_out,
       not_12_out, not_13_out;

  Clock clock_1 (.out(clock_1_out));
  D_Flip_Flop d_ff_1 (
    .clk(clock_1_out), .D(d_ff_1_qn), .Q(d_ff_1_q), .Qn(d_ff_1_qn), .reset(and_1_out));  // open: preset, en
  D_Flip_Flop d_ff_2 (
    .clk(and_1_out), .D(d_ff_2_qn), .Q(d_ff_2_q), .Qn(d_ff_2_qn), .reset(and_2_out));  // open: preset, en
  D_Flip_Flop d_ff_3 (
    .clk(d_ff_4_qn), .D(d_ff_3_qn), .Q(d_ff_3_q), .Qn(d_ff_3_qn), .reset(and_1_out));  // open: preset, en
  D_Flip_Flop d_ff_4 (
    .clk(d_ff_1_qn), .D(d_ff_4_qn), .Q(d_ff_4_q), .Qn(d_ff_4_qn), .reset(and_1_out));  // open: preset, en
  D_Flip_Flop d_ff_5 (
    .clk(d_ff_2_qn), .D(d_ff_5_qn), .Q(d_ff_5_q), .Qn(d_ff_5_qn), .reset(and_2_out));  // open: preset, en
  D_Flip_Flop d_ff_6 (
    .clk(d_ff_3_qn), .D(d_ff_6_qn), .Q(d_ff_6_q), .Qn(d_ff_6_qn), .reset(and_1_out));  // open: preset, en
  D_Flip_Flop d_ff_7 (
    .clk(d_ff_5_qn), .D(d_ff_7_qn), .Q(d_ff_7_q), .Qn(d_ff_7_qn), .reset(and_2_out));  // open: preset, en
  and and_1 (and_1_out, d_ff_4_q, d_ff_6_q);
  and and_2 (and_2_out, d_ff_7_q, d_ff_5_q);
  not nD (nD_out, d_ff_1_q);
  not nC (nC_out, d_ff_4_q);
  not nB (nB_out, d_ff_3_q);
  not not_1 (not_1_out, d_ff_2_q);
  not not_2 (not_2_out, d_ff_5_q);
  not not_3 (not_3_out, d_ff_7_q);
  or A (A_out, BD_out, nB_nD_out, d_ff_6_q, d_ff_4_q);
  and BD (BD_out, d_ff_3_q, d_ff_1_q);
  and nB_nD (nB_nD_out, nB_out, nD_out);
  or A_2 (A_2_out, BD_2_out, nB_nD_2_out, d_ff_5_q);
  and BD_2 (BD_2_out, d_ff_7_q, d_ff_2_q);
  and nB_nD_2 (nB_nD_2_out, not_3_out, not_1_out);
  or B (B_out, CD_out, nC_nD_out, nB_out);
  and nC_nD (nC_nD_out, nC_out, nD_out);
  and CD (CD_out, d_ff_4_q, d_ff_1_q);
  or B_2 (B_2_out, CD_2_out, nC_nD_2_out, not_3_out);
  and nC_nD_2 (nC_nD_2_out, not_2_out, not_1_out);
  and CD_2 (CD_2_out, d_ff_5_q, d_ff_2_q);
  or F (F_out, nC_nD_3_out, B_nD_out, B_nC_out, d_ff_6_q);
  and B_nD (B_nD_out, d_ff_3_q, nD_out);
  and nC_nD_3 (nC_nD_3_out, nC_out, nD_out);
  and nC_nD_4 (nC_nD_4_out, not_2_out, not_1_out);
  _7_Segment_Display u_7_segment_display_1 (
    .g(G_out), .f(F_out), .a(A_out), .b(B_out), .e(E_out), .d(D_out), .c(C_out));  // open: dp
  or G (G_out, C_nD_out, B_nC_out, d_ff_6_q, nBC_out);
  and C_nD (C_nD_out, d_ff_4_q, nD_out);
  _7_Segment_Display u_7_segment_display_2 (
    .g(G_2_out), .f(F_2_out), .a(A_2_out), .b(B_2_out), .e(E_2_out), .d(D_2_out), .c(C_2_out));  // open: dp
  or F_2 (F_2_out, nC_nD_4_out, B_nD_2_out, B_nC_2_out);
  or G_2 (G_2_out, C_nD_2_out, B_nC_2_out, nBC_2_out);
  and C_nD_2 (C_nD_2_out, d_ff_5_q, not_1_out);
  and B_nD_2 (B_nD_2_out, d_ff_7_q, not_1_out);
  and nBC (nBC_out, nB_out, d_ff_4_q);
  and nBC_2 (nBC_2_out, not_3_out, d_ff_5_q);
  or C (C_out, d_ff_3_q, nC_out, d_ff_1_q);
  and C_nD_3 (C_nD_3_out, d_ff_4_q, nD_out);
  or C_2 (C_2_out, d_ff_7_q, not_2_out, d_ff_2_q);
  or E (E_out, C_nD_3_out, nB_nD_3_out);
  or D (D_out, d_ff_6_q, C_nD_3_out, nBC_3_out, nB_nD_3_out, nB_nCD_out);
  and nBC_3 (nBC_3_out, nB_out, d_ff_4_q);
  and nB_nCD (nB_nCD_out, d_ff_1_q, B_nC_out);
  and nB_nD_3 (nB_nD_3_out, nB_out, nD_out);
  or D_2 (D_2_out, C_nD_4_out, nBC_4_out, nB_nD_4_out, nB_nCD_2_out);
  and C_nD_4 (C_nD_4_out, d_ff_5_q, not_1_out);
  and nB_nD_4 (nB_nD_4_out, not_3_out, not_1_out);
  and nBC_4 (nBC_4_out, not_3_out, d_ff_5_q);
  and B_nC (B_nC_out, nC_out, d_ff_3_q);
  or E_2 (E_2_out, C_nD_4_out, nB_nD_4_out);
  and nB_nCD_2 (nB_nCD_2_out, d_ff_2_q, B_nC_2_out);
  and B_nC_2 (B_nC_2_out, not_2_out, d_ff_7_q);
  D_Flip_Flop d_ff_8 (
    .clk(and_2_out), .D(d_ff_8_qn), .Q(d_ff_8_q), .Qn(d_ff_8_qn), .reset(and_3_out));  // open: preset, en
  D_Flip_Flop d_ff_9 (
    .clk(and_3_out), .D(d_ff_9_qn), .Q(d_ff_9_q), .Qn(d_ff_9_qn), .reset(and_4_out));  // open: preset, en
  D_Flip_Flop d_ff_10 (
    .clk(d_ff_8_qn), .D(d_ff_10_qn), .Q(d_ff_10_q), .Qn(d_ff_10_qn), .reset(and_3_out));  // open: preset, en
  D_Flip_Flop d_ff_11 (
    .clk(d_ff_10_qn), .D(d_ff_11_qn), .Q(d_ff_11_q), .Qn(d_ff_11_qn), .reset(and_3_out));  // open: preset, en
  D_Flip_Flop d_ff_12 (
    .clk(d_ff_9_qn), .D(d_ff_12_qn), .Q(d_ff_12_q), .Qn(d_ff_12_qn), .reset(and_4_out));  // open: preset, en
  D_Flip_Flop d_ff_13 (
    .clk(d_ff_11_qn), .D(d_ff_13_qn), .Q(d_ff_13_q), .Qn(d_ff_13_qn), .reset(and_3_out));  // open: preset, en
  D_Flip_Flop d_ff_14 (
    .clk(d_ff_12_qn), .D(d_ff_14_qn), .Q(d_ff_14_q), .Qn(d_ff_14_qn), .reset(and_4_out));  // open: preset, en
  and and_3 (and_3_out, d_ff_10_q, d_ff_13_q);
  and and_4 (and_4_out, d_ff_14_q, d_ff_12_q);
  not not_4 (not_4_out, d_ff_8_q);
  not not_5 (not_5_out, d_ff_10_q);
  not not_6 (not_6_out, d_ff_11_q);
  not not_7 (not_7_out, d_ff_9_q);
  not not_8 (not_8_out, d_ff_12_q);
  not not_9 (not_9_out, d_ff_14_q);
  or A_3 (A_3_out, BD_3_out, nB_nD_5_out, d_ff_13_q, d_ff_10_q);
  and BD_3 (BD_3_out, d_ff_11_q, d_ff_8_q);
  and nB_nD_5 (nB_nD_5_out, not_6_out, not_4_out);
  or A_4 (A_4_out, BD_4_out, nB_nD_6_out, d_ff_12_q);
  and nB_nD_6 (nB_nD_6_out, not_9_out, not_7_out);
  and BD_4 (BD_4_out, d_ff_14_q, d_ff_9_q);
  or B_3 (B_3_out, CD_3_out, nC_nD_5_out, not_6_out);
  and CD_3 (CD_3_out, d_ff_10_q, d_ff_8_q);
  and nC_nD_5 (nC_nD_5_out, not_5_out, not_4_out);
  or B_4 (B_4_out, CD_4_out, nC_nD_6_out, not_9_out);
  and nC_nD_6 (nC_nD_6_out, not_8_out, not_7_out);
  and CD_4 (CD_4_out, d_ff_12_q, d_ff_9_q);
  or F_3 (F_3_out, nC_nD_7_out, B_nD_3_out, B_nC_3_out, d_ff_13_q);
  and nC_nD_7 (nC_nD_7_out, not_5_out, not_4_out);
  and B_nD_3 (B_nD_3_out, d_ff_11_q, not_4_out);
  and nC_nD_8 (nC_nD_8_out, not_8_out, not_7_out);
  _7_Segment_Display u_7_segment_display_3 (
    .g(G_3_out), .f(F_3_out), .a(A_3_out), .b(B_3_out), .e(E_3_out), .d(D_3_out), .c(C_3_out));  // open: dp
  or G_3 (G_3_out, C_nD_5_out, B_nC_3_out, d_ff_13_q, nBC_5_out);
  and C_nD_5 (C_nD_5_out, d_ff_10_q, not_4_out);
  _7_Segment_Display u_7_segment_display_4 (
    .g(G_4_out), .f(F_4_out), .a(A_4_out), .b(B_4_out), .e(E_4_out), .d(D_4_out), .c(C_4_out));  // open: dp
  or F_4 (F_4_out, nC_nD_8_out, B_nD_4_out, B_nC_4_out);
  or G_4 (G_4_out, C_nD_6_out, B_nC_4_out, nBC_6_out);
  and C_nD_6 (C_nD_6_out, d_ff_12_q, not_7_out);
  and B_nD_4 (B_nD_4_out, d_ff_14_q, not_7_out);
  and nBC_5 (nBC_5_out, not_6_out, d_ff_10_q);
  and nBC_6 (nBC_6_out, not_9_out, d_ff_12_q);
  or C_3 (C_3_out, d_ff_11_q, not_5_out, d_ff_8_q);
  and C_nD_7 (C_nD_7_out, d_ff_10_q, not_4_out);
  or C_4 (C_4_out, d_ff_14_q, not_8_out, d_ff_9_q);
  or E_3 (E_3_out, C_nD_7_out, nB_nD_7_out);
  or D_3 (D_3_out, d_ff_13_q, C_nD_7_out, nBC_7_out, nB_nD_7_out, nB_nCD_3_out);
  and nB_nCD_3 (nB_nCD_3_out, d_ff_8_q, B_nC_3_out);
  and nB_nD_7 (nB_nD_7_out, not_6_out, not_4_out);
  and nBC_7 (nBC_7_out, not_6_out, d_ff_10_q);
  or D_4 (D_4_out, C_nD_8_out, nBC_8_out, nB_nD_8_out, nB_nCD_4_out);
  and C_nD_8 (C_nD_8_out, d_ff_12_q, not_7_out);
  and nBC_8 (nBC_8_out, not_9_out, d_ff_12_q);
  and nB_nD_8 (nB_nD_8_out, not_9_out, not_7_out);
  and B_nC_3 (B_nC_3_out, not_5_out, d_ff_11_q);
  or E_4 (E_4_out, C_nD_8_out, nB_nD_8_out);
  and nB_nCD_4 (nB_nCD_4_out, d_ff_9_q, B_nC_4_out);
  and B_nC_4 (B_nC_4_out, not_8_out, d_ff_14_q);
  D_Flip_Flop d_ff_15 (
    .clk(and_4_out), .D(d_ff_15_qn), .Q(d_ff_15_q), .Qn(d_ff_15_qn), .reset(and_6_out));  // open: preset, en
  D_Flip_Flop d_ff_16 (
    .clk(d_ff_15_qn), .D(d_ff_16_qn), .Q(d_ff_16_q), .Qn(d_ff_16_qn), .reset(and_6_out));  // open: preset, en
  D_Flip_Flop d_ff_17 (
    .clk(d_ff_16_qn), .D(d_ff_17_qn), .Q(d_ff_17_q), .Qn(d_ff_17_qn), .reset(and_6_out));  // open: preset, en
  and and_5 (and_5_out, d_ff_16_q, d_ff_18_q);
  and and_6 (and_6_out, d_ff_17_q, d_ff_18_q);
  D_Flip_Flop d_ff_18 (
    .clk(d_ff_17_qn), .D(d_ff_18_qn), .Q(d_ff_18_q), .Qn(d_ff_18_qn), .reset(and_6_out));  // open: preset, en
  not not_10 (not_10_out, d_ff_15_q);
  not not_11 (not_11_out, d_ff_16_q);
  not not_12 (not_12_out, d_ff_17_q);
  not not_13 (not_13_out, d_ff_18_q);
  and nAC (nAC_out, not_13_out, d_ff_16_q);
  and A_nC (A_nC_out, d_ff_18_q, not_11_out);
  or A_5 (A_5_out, nAC_out, A_nC_out, BC_out, BD_5_out, nB_nD_9_out);
  and BC (BC_out, d_ff_17_q, d_ff_16_q);
  and nB_nD_9 (nB_nD_9_out, not_12_out, not_10_out);
  and BD_5 (BD_5_out, d_ff_17_q, d_ff_15_q);
  or B_5 (B_5_out, d_ff_18_q, CD_5_out, nC_nD_9_out, not_12_out);
  and nC_nD_9 (nC_nD_9_out, not_11_out, not_10_out);
  and CD_5 (CD_5_out, d_ff_16_q, d_ff_15_q);
  and nC_nD_10 (nC_nD_10_out, not_11_out, not_10_out);
  and A_nD (A_nD_out, d_ff_18_q, not_10_out);
  or F_5 (F_5_out, A_nD_out, nC_nD_10_out, B_nD_5_out, B_nC_6_out, A_nC_2_out);
  and B_nC_5 (B_nC_5_out, d_ff_17_q, not_11_out);
  and B_nD_5 (B_nD_5_out, d_ff_17_q, not_10_out);
  D_Flip_Flop d_ff_19 (.clk(and_5_out), .D(d_ff_19_qn), .Qn(d_ff_19_qn), .reset(and_6_out));  // open: Q, preset, en
  _7_Segment_Display u_7_segment_display_5 (
    .g(G_5_out), .f(F_5_out), .a(A_5_out), .b(B_5_out), .e(E_5_out), .d(D_5_out), .c(C_5_out));  // open: dp
  or G_5 (G_5_out, B_nC_5_out, B_nD_6_out, A_nC_2_out, nA_nBC_out);
  and B_nD_6 (B_nD_6_out, d_ff_17_q, not_10_out);
  _7_Segment_Display u_7_segment_display_6 (
    .f(d_ff_19_qn), .a(d_ff_19_qn), .b(1'b1), .e(d_ff_19_qn), .d(d_ff_19_qn), .c(1'b1));  // open: g, dp
  or C_5 (C_5_out, d_ff_18_q, d_ff_17_q, not_11_out, d_ff_15_q);
  and C_nD_9 (C_nD_9_out, d_ff_16_q, not_10_out);
  and A_nC_2 (A_nC_2_out, d_ff_18_q, not_11_out);
  or E_5 (E_5_out, C_nD_9_out, nB_nD_10_out);
  or D_5 (D_5_out, A_nC_2_out, C_nD_9_out, nA_nBC_out, nB_nD_10_out, nB_nCD_5_out);
  and nB_nD_10 (nB_nD_10_out, not_12_out, not_10_out);
  and nA_nBC (nA_nBC_out, not_12_out, not_13_out, d_ff_16_q);
  and nB_nCD_5 (nB_nCD_5_out, d_ff_15_q, B_nC_6_out);
  and B_nC_6 (B_nC_6_out, not_11_out, d_ff_17_q);
endmodule
